# Fritzing sketch schematic (saved by Fritzing 0.9.4)
breadboards: 1

parts:
  TP1 = TP4056 [chip_label=TP4056 package="DIP (Dual Inline) [THT]"]
  U1 = W5100 mini [package=W5100]
  OLED_I2C1 = OLED 128x64 I2C Monochrome Display
  Componente2 = Arduino Nano (Rev3.0)
  BAT1 = Battery Holders [package=lipo-1100mAh]

nets:
  VCC: TP1.pin3, U1.VCC, OLED_I2C1.VDD, Componente2.5V
  N1: TP1.pin4, BAT1.+
  N2: TP1.pin5, BAT1.-
  GND: TP1.pin6, U1.GND, OLED_I2C1.GND, Componente2.GND
  N3: U1.MOSI, Componente2.D11/MOSI
  N4: U1.MISO, Componente2.D12/MISO
  N5: U1.RESET, Componente2.D4
  N6: U1.SCK, Componente2.D13/SCK
  N7: U1.SS, Componente2.D10
  N8: OLED_I2C1.SDA, Componente2.A4
  N9: OLED_I2C1.SCK, Componente2.A5

custom parts:
  TP4056: A DIP stand-in part for whatever IC you want. With 6 pins on a 300mil dual inline package (DIP) footprint.
  W5100 mini: WIZnet W5100 Network Module Mini
